// Digital circuit 3-to-8 Decoder.dig as structural Verilog
module _3_to_8_Decoder (
  input  S0,
  input  S1,
  input  S2,
  input  Data,
  output O0,
  output O1,
  output O2,
  output O3,
  output O4,
  output O5,
  output O6,
  output O7
);

  wire not_1_out, not_2_out, not_3_out;

  not not_1 (not_1_out, S0);
  not not_2 (not_2_out, S1);
  not not_3 (not_3_out, S2);
  and and_1 (O0, Data, not_1_out, not_2_out, not_3_out);
  and and_2 (O1, Data, S0, not_2_out, not_3_out);
  and and_3 (O2, Data, S1, not_1_out, not_3_out);
  and and_4 (O3, Data, S0, S1, not_3_out);
  and and_5 (O4, Data, S2, not_1_out, not_2_out);
  and and_6 (O5, Data, S0, S2, not_2_out);
  and and_7 (O6, Data, S1, S2, not_1_out);
  and and_8 (O7, Data, S0, S1, S2);
endmodule
