// Digital circuit 3-to-8-line-decoder.dig as structural Verilog
module _3_to_8_line_decoder (
  input  I0,
  input  D,
  input  I1,
  output O0,
  output O1,
  output O2,
  output O3
);

  wire not_1_out, not_2_out;

  not not_1 (not_1_out, I1);
  not not_2 (not_2_out, I0);
  and and_1 (O0, D, I1, I0);
  and and_2 (O1, D, I1, not_2_out);
  and and_3 (O2, D, I0, not_1_out);
  and and_4 (O3, D, not_1_out, not_2_out);
endmodule
