// Digital circuit 8-bit latch_Clear.dig as structural Verilog
module _8_bit_latch_Clear (
  input  I0,
  input  I1,
  input  I2,
  input  I3,
  input  I4,
  input  I5,
  input  I6,
  input  I7,
  input  Clear,
  input  CLK,
  output O0,
  output O1,
  output O2,
  output O3,
  output O4,
  output O5,
  output O6,
  output O7
);

  leve_triggered_D_type_flip_flop leve_triggered_d_type_flip_flop_1 (
    .Clear(Clear), .Clock(CLK), .Data(I7), .Q(O7));  // open: Q_2
  leve_triggered_D_type_flip_flop leve_triggered_d_type_flip_flop_2 (
    .Clear(Clear), .Clock(CLK), .Data(I6), .Q(O6));  // open: Q_2
  leve_triggered_D_type_flip_flop leve_triggered_d_type_flip_flop_3 (
    .Clear(Clear), .Clock(CLK), .Data(I5), .Q(O5));  // open: Q_2
  leve_triggered_D_type_flip_flop leve_triggered_d_type_flip_flop_4 (
    .Clear(Clear), .Clock(CLK), .Data(I4), .Q(O4));  // open: Q_2
  leve_triggered_D_type_flip_flop leve_triggered_d_type_flip_flop_5 (
    .Clear(Clear), .Clock(CLK), .Data(I3), .Q(O3));  // open: Q_2
  leve_triggered_D_type_flip_flop leve_triggered_d_type_flip_flop_6 (
    .Clear(Clear), .Clock(CLK), .Data(I2), .Q(O2));  // open: Q_2
  leve_triggered_D_type_flip_flop leve_triggered_d_type_flip_flop_7 (
    .Clear(Clear), .Clock(CLK), .Data(I1), .Q(O1));  // open: Q_2
  leve_triggered_D_type_flip_flop leve_triggered_d_type_flip_flop_8 (
    .Clear(Clear), .Clock(CLK), .Data(I0), .Q(O0));  // open: Q_2
endmodule
