// Digital circuit 8-to-1 Selector.dig as structural Verilog
module _8_to_1_Selector (
  input  D0,
  input  D1,
  input  D2,
  input  D3,
  input  D4,
  input  D5,
  input  D6,
  input  D7,
  input  S0,
  input  S1,
  input  S2,
  output Out
);

  wire and_1_out, and_2_out, and_3_out, and_4_out, and_5_out, and_6_out, and_7_out, and_8_out, not_1_out,
       not_2_out, not_3_out;

  not not_1 (not_1_out, S0);
  not not_2 (not_2_out, S1);
  not not_3 (not_3_out, S2);
  and and_1 (and_1_out, D0, not_1_out, not_2_out, not_3_out);
  and and_2 (and_2_out, D1, S0, not_2_out, not_3_out);
  and and_3 (and_3_out, D2, S1, not_1_out, not_3_out);
  and and_4 (and_4_out, D3, S0, S1, not_3_out);
  and and_5 (and_5_out, D4, S2, not_1_out, not_2_out);
  and and_6 (and_6_out, D5, S0, S2, not_2_out);
  and and_7 (and_7_out, D6, S1, S2, not_1_out);
  and and_8 (and_8_out, D7, S0, S1, S2);
  or or_1 (Out, and_1_out, and_2_out, and_3_out, and_4_out, and_5_out, and_6_out, and_7_out, and_8_out);
endmodule
