// Digital circuit 8X1 RAM.dig as structural Verilog
module _8X1_RAM (
  input  A0,
  input  A1,
  input  A2,
  input  DI,
  input  W,
  output DO
);

  wire _3_to_8_decoder_1_o0, _3_to_8_decoder_1_o1, _3_to_8_decoder_1_o2, _3_to_8_decoder_1_o3,
       _3_to_8_decoder_1_o4, _3_to_8_decoder_1_o5, _3_to_8_decoder_1_o6, _3_to_8_decoder_1_o7,
       flip_flop_latch_1_do, flip_flop_latch_2_do, flip_flop_latch_3_do, flip_flop_latch_4_do,
       flip_flop_latch_5_do, flip_flop_latch_6_do, flip_flop_latch_7_do, flip_flop_latch_8_do;

  flip_flop_latch flip_flop_latch_1 (.DI(DI), .W(_3_to_8_decoder_1_o7), .DO(flip_flop_latch_1_do));
  flip_flop_latch flip_flop_latch_2 (.DI(DI), .W(_3_to_8_decoder_1_o6), .DO(flip_flop_latch_2_do));
  flip_flop_latch flip_flop_latch_3 (.DI(DI), .W(_3_to_8_decoder_1_o5), .DO(flip_flop_latch_3_do));
  flip_flop_latch flip_flop_latch_4 (.DI(DI), .W(_3_to_8_decoder_1_o4), .DO(flip_flop_latch_4_do));
  _3_to_8_Decoder _3_to_8_decoder_1 (
    .S0(W), .S1(A0), .S2(A1), .Data(A2), .O0(_3_to_8_decoder_1_o0), .O1(_3_to_8_decoder_1_o1),
    .O2(_3_to_8_decoder_1_o2), .O3(_3_to_8_decoder_1_o3), .O4(_3_to_8_decoder_1_o4),
    .O5(_3_to_8_decoder_1_o5), .O6(_3_to_8_decoder_1_o6), .O7(_3_to_8_decoder_1_o7));
  flip_flop_latch flip_flop_latch_5 (.DI(DI), .W(_3_to_8_decoder_1_o3), .DO(flip_flop_latch_5_do));
  flip_flop_latch flip_flop_latch_6 (.DI(DI), .W(_3_to_8_decoder_1_o2), .DO(flip_flop_latch_6_do));
  _8_to_1_Selector _8_to_1_selector_1 (
    .D0(flip_flop_latch_8_do), .D1(flip_flop_latch_7_do), .D2(flip_flop_latch_6_do),
    .D3(flip_flop_latch_5_do), .D4(flip_flop_latch_4_do), .D5(flip_flop_latch_3_do),
    .D6(flip_flop_latch_2_do), .D7(flip_flop_latch_1_do), .S0(A0), .S1(A1), .S2(A2), .Out(DO));
  flip_flop_latch flip_flop_latch_7 (.DI(DI), .W(_3_to_8_decoder_1_o1), .DO(flip_flop_latch_7_do));
  flip_flop_latch flip_flop_latch_8 (.DI(DI), .W(_3_to_8_decoder_1_o0), .DO(flip_flop_latch_8_do));
endmodule
