// Digital circuit 8bit-latch.dig as structural Verilog
module _8bit_latch (
  input  DI0,
  input  DI1,
  input  DI2,
  input  DI3,
  input  DI4,
  input  DI5,
  input  DI6,
  input  DI7,
  input  Write,
  output DO0,
  output DO1,
  output DO2,
  output DO3,
  output DO4,
  output DO5,
  output DO6,
  output D07
);

  flip_flop_latch flip_flop_latch_1 (.DI(DI7), .W(Write), .DO(D07));
  flip_flop_latch flip_flop_latch_2 (.DI(DI6), .W(Write), .DO(DO6));
  flip_flop_latch flip_flop_latch_3 (.DI(DI5), .W(Write), .DO(DO5));
  flip_flop_latch flip_flop_latch_4 (.DI(DI4), .W(Write), .DO(DO4));
  flip_flop_latch flip_flop_latch_5 (.DI(DI3), .W(Write), .DO(DO3));
  flip_flop_latch flip_flop_latch_6 (.DI(DI2), .W(Write), .DO(DO2));
  flip_flop_latch flip_flop_latch_7 (.DI(DI1), .W(Write), .DO(DO1));
  flip_flop_latch flip_flop_latch_8 (.DI(DI0), .W(Write), .DO(DO0));
endmodule
