// Digital circuit 8bitAdder.dig as structural Verilog
module _8bitAdder (
  input  Ci,
  input  A0,
  input  A1,
  input  A2,
  input  A3,
  input  A4,
  input  A5,
  input  A6,
  input  A7,
  input  B0,
  input  B1,
  input  B2,
  input  B3,
  input  B4,
  input  B5,
  input  B6,
  input  B7,
  output O0,
  output O1,
  output O2,
  output O3,
  output O4,
  output O5,
  output O6,
  output O7,
  output Co
);

  wire fulladder_1_co, fulladder_2_co, fulladder_3_co, fulladder_4_co, fulladder_5_co, fulladder_6_co,
       fulladder_7_co;

  fullAdder fulladder_1 (.Ci(Ci), .A(A0), .B(B0), .S(O0), .co(fulladder_1_co));
  fullAdder fulladder_2 (.Ci(fulladder_1_co), .A(A1), .B(B1), .S(O1), .co(fulladder_2_co));
  fullAdder fulladder_3 (.Ci(fulladder_2_co), .A(A2), .B(B2), .S(O2), .co(fulladder_3_co));
  fullAdder fulladder_4 (.Ci(fulladder_3_co), .A(A3), .B(B3), .S(O3), .co(fulladder_4_co));
  fullAdder fulladder_5 (.Ci(fulladder_4_co), .A(A4), .B(B4), .S(O4), .co(fulladder_5_co));
  fullAdder fulladder_6 (.Ci(fulladder_5_co), .A(A5), .B(B5), .S(O5), .co(fulladder_6_co));
  fullAdder fulladder_7 (.Ci(fulladder_6_co), .A(A6), .B(B6), .S(O6), .co(fulladder_7_co));
  fullAdder fulladder_8 (.Ci(fulladder_7_co), .A(A7), .B(B7), .S(O7), .co(Co));
endmodule
