// Digital circuit 8bitSubtractor.dig as structural Verilog
module _8bitSubtractor (
  input  in_1,
  input  in_2,
  input  in_3,
  input  in_4,
  input  in_5,
  input  in_6,
  input  in_7,
  input  in_8,
  input  in_9,
  input  in_10,
  input  in_11,
  input  in_12,
  input  in_13,
  input  in_14,
  input  in_15,
  input  in_16,
  input  in_17
);

  wire _8bitadder_1_o5, undriven, undriven_2, undriven_3, undriven_4, undriven_5, undriven_6, undriven_7,
       undriven_8, xor_1_out, xor_2_out, xor_3_out, xor_4_out, xor_5_out, xor_6_out, xor_7_out, xor_8_out;

  LED led_1 (.in(undriven));
  LED led_2 (.in(undriven_2));
  LED led_3 (.in(undriven_3));
  LED led_4 (.in(_8bitadder_1_o5));
  xor xor_1 (xor_1_out, in_1, in_2);
  LED led_5 (.in(undriven_4));
  LED led_6 (.in(undriven_5));
  xor xor_2 (xor_2_out, in_1, in_3);
  LED led_7 (.in(undriven_6));
  LED led_8 (.in(undriven_7));
  xor xor_3 (xor_3_out, in_1, in_4);
  _8bitAdder _8bitadder_1 (
    .Ci(in_1), .A0(xor_8_out), .A1(xor_7_out), .A2(xor_6_out), .A3(xor_5_out), .A4(xor_4_out),
    .A5(xor_3_out), .A6(xor_2_out), .A7(xor_1_out), .B0(in_17), .B1(in_16), .B2(in_15), .B3(in_14),
    .B4(in_13), .B5(in_12), .B6(in_11), .B7(in_10), .O5(_8bitadder_1_o5));  // open: O0, O1, O2, O3, O4, O6, O7, Co
  LED led_9 (.in(undriven_8));
  xor xor_4 (xor_4_out, in_1, in_5);
  xor xor_5 (xor_5_out, in_1, in_6);
  xor xor_6 (xor_6_out, in_1, in_7);
  xor xor_7 (xor_7_out, in_1, in_8);
  xor xor_8 (xor_8_out, in_1, in_9);
endmodule
