// Digital circuit counter.dig as structural Verilog
module counter (
  input  Clk,
  output Q0,
  output Q1,
  output Q2,
  output Q3,
  output Q4,
  output Q5,
  output Q6,
  output Q7
);

  wire edge_triggered_d_type_flip_flop_1_q_2, edge_triggered_d_type_flip_flop_2_q_2,
       edge_triggered_d_type_flip_flop_3_q_2, edge_triggered_d_type_flip_flop_4_q_2,
       edge_triggered_d_type_flip_flop_5_q_2, edge_triggered_d_type_flip_flop_6_q_2,
       edge_triggered_d_type_flip_flop_7_q_2, edge_triggered_d_type_flip_flop_8_q_2;

  edge_triggered_d_type_flip_flop edge_triggered_d_type_flip_flop_1 (
    .D(edge_triggered_d_type_flip_flop_1_q_2), .CLK(Clk), .Q(Q0), .Q_2(edge_triggered_d_type_flip_flop_1_q_2));
  edge_triggered_d_type_flip_flop edge_triggered_d_type_flip_flop_2 (
    .D(edge_triggered_d_type_flip_flop_2_q_2), .CLK(edge_triggered_d_type_flip_flop_1_q_2), .Q(Q1),
    .Q_2(edge_triggered_d_type_flip_flop_2_q_2));
  edge_triggered_d_type_flip_flop edge_triggered_d_type_flip_flop_3 (
    .D(edge_triggered_d_type_flip_flop_3_q_2), .CLK(edge_triggered_d_type_flip_flop_2_q_2), .Q(Q2),
    .Q_2(edge_triggered_d_type_flip_flop_3_q_2));
  edge_triggered_d_type_flip_flop edge_triggered_d_type_flip_flop_4 (
    .D(edge_triggered_d_type_flip_flop_4_q_2), .CLK(edge_triggered_d_type_flip_flop_3_q_2), .Q(Q3),
    .Q_2(edge_triggered_d_type_flip_flop_4_q_2));
  edge_triggered_d_type_flip_flop edge_triggered_d_type_flip_flop_5 (
    .D(edge_triggered_d_type_flip_flop_5_q_2), .CLK(edge_triggered_d_type_flip_flop_4_q_2), .Q(Q4),
    .Q_2(edge_triggered_d_type_flip_flop_5_q_2));
  edge_triggered_d_type_flip_flop edge_triggered_d_type_flip_flop_6 (
    .D(edge_triggered_d_type_flip_flop_6_q_2), .CLK(edge_triggered_d_type_flip_flop_5_q_2), .Q(Q5),
    .Q_2(edge_triggered_d_type_flip_flop_6_q_2));
  edge_triggered_d_type_flip_flop edge_triggered_d_type_flip_flop_7 (
    .D(edge_triggered_d_type_flip_flop_7_q_2), .CLK(edge_triggered_d_type_flip_flop_6_q_2), .Q(Q6),
    .Q_2(edge_triggered_d_type_flip_flop_7_q_2));
  edge_triggered_d_type_flip_flop edge_triggered_d_type_flip_flop_8 (
    .D(edge_triggered_d_type_flip_flop_8_q_2), .CLK(edge_triggered_d_type_flip_flop_7_q_2), .Q(Q7),
    .Q_2(edge_triggered_d_type_flip_flop_8_q_2));
endmodule
