// Digital circuit edge_triggered_d_type_flip_flop.dig as structural Verilog
module edge_triggered_d_type_flip_flop (
  input  D,
  input  CLK,
  output Q,
  output Q_2
);

  wire and_1_out, and_2_out, and_3_out, and_4_out, nor_1_out, nor_2_out, not_1_out, not_2_out;

  not not_1 (not_1_out, CLK);
  not not_2 (not_2_out, D);
  and and_1 (and_1_out, D, not_1_out);
  and and_2 (and_2_out, not_1_out, not_2_out);
  nor nor_1 (nor_1_out, and_1_out, nor_2_out);
  nor nor_2 (nor_2_out, nor_1_out, and_2_out);
  and and_3 (and_3_out, nor_1_out, CLK);
  and and_4 (and_4_out, CLK, nor_2_out);
  nor nor_3 (Q, and_3_out, Q_2);
  nor nor_4 (Q_2, Q, and_4_out);
endmodule
