// Digital circuit flip_flop_latch.dig as structural Verilog
module flip_flop_latch (
  input  DI,
  input  W,
  output DO
);

  wire and_1_out, and_2_out, nor_2_out, not_1_out;

  not not_1 (not_1_out, DI);
  and and_1 (and_1_out, not_1_out, W);
  and and_2 (and_2_out, W, DI);
  nor nor_1 (DO, and_1_out, nor_2_out);
  nor nor_2 (nor_2_out, DO, and_2_out);
endmodule
