// Digital circuit full_adder.dig as structural Verilog
module full_adder (
  input  A,
  input  B,
  input  Carry,
  output Sum,
  output Carry_2
);

  wire and_1_out, and_2_out, xor_1_out;

  xor xor_1 (xor_1_out, A, B);
  and and_1 (and_1_out, A, B);
  xor xor_2 (Sum, Carry, xor_1_out);
  and and_2 (and_2_out, Carry, xor_1_out);
  or or_1 (Carry_2, and_2_out, and_1_out);
  // full_adder full_adder_1: pin names not known
endmodule
