// Digital circuit leve-triggered D-type flip-flop.dig as structural Verilog
module leve_triggered_D_type_flip_flop (
  input  Clock,
  input  Data,
  input  Clear,
  output Q,
  output Q_2
);

  wire and_1_out, and_2_out, not_1_out, or_1_out;

  not not_1 (not_1_out, Data);
  and and_1 (and_1_out, not_1_out, Clock);
  and and_2 (and_2_out, Clock, Data);
  or or_1 (or_1_out, Clear, and_1_out);
  nor nor_1 (Q, or_1_out, Q_2);
  nor nor_2 (Q_2, Q, and_2_out);
endmodule
