// Digital circuit te.dig as structural Verilog
module te (
  input  clk,
  output A1,
  output A2,
  output A3,
  output A4,
  output A5,
  output A6,
  output A7,
  output A0
);

  // ScopeTrigger scopetrigger_1: pin names not known; wires that end beside it: clk
  counter counter_1 (.Clk(clk), .Q0(A0), .Q1(A1), .Q2(A2), .Q3(A3), .Q4(A4), .Q5(A5), .Q6(A6), .Q7(A7));

  // Notes on the sheet:
  //   clk: Hz: 10
endmodule
