// Digital circuit test.dig as structural Verilog
module test (
  input  in_1,
  input  in_2,
  input  in_3,
  input  in_4,
  input  in_5,
  input  in_6,
  input  in_7,
  input  in_8,
  input  Clear,
  input  CLK,
  output out_10,
  output out_11,
  output out_12,
  output out_13,
  output out_14,
  output out_15,
  output out_16,
  output out_17,
  output out_18
);

  wire _8bitadder_1_o0, _8bitadder_1_o1, _8bitadder_1_o2, _8bitadder_1_o3, _8bitadder_1_o4, _8bitadder_1_o5,
       _8bitadder_1_o6, _8bitadder_1_o7;

  _8bitAdder _8bitadder_1 (
    .Ci(1'b0), .A0(out_17), .A1(out_16), .A2(out_15), .A3(out_14), .A4(out_13), .A5(out_12), .A6(out_11),
    .A7(out_10), .B0(in_1), .B1(in_2), .B2(in_3), .B3(in_4), .B4(in_5), .B5(in_6), .B6(in_7), .B7(in_8),
    .O0(_8bitadder_1_o0), .O1(_8bitadder_1_o1), .O2(_8bitadder_1_o2), .O3(_8bitadder_1_o3),
    .O4(_8bitadder_1_o4), .O5(_8bitadder_1_o5), .O6(_8bitadder_1_o6), .O7(_8bitadder_1_o7), .Co(out_18));
  // _8_bit_latch _8_bit_latch_1: pin names not known; wires that end beside it: CLK, Clear, _8bitadder_1_o7, out_10, _8bitadder_1_o6, out_11, _8bitadder_1_o5, out_12, _8bitadder_1_o4, out_13, _8bitadder_1_o3, out_14, _8bitadder_1_o2, out_15, _8bitadder_1_o1, out_16, _8bitadder_1_o0, out_17
endmodule
